# Fritzing sketch rgbLedFritzing (saved by Fritzing 0.9.3b)
breadboards: 1

parts:
  Q1 = TRANSISTOR_NPN [package=to-92-ammo]
  Q2 = TRANSISTOR_NPN [package=to-92-ammo]
  Q3 = TRANSISTOR_NPN [package=to-92-ammo]
  LED2 = RGB LED (com. cathode, rbg) [package="5 mm [THT]"]
  Componente1 = Arduino Board Ethernet
  Componente2 = RFID-RC522-v2

nets:
  GND: Q1.E, Q2.E, Q3.E, Componente1.GND, Componente2.GND
  N1: Q1.B, Componente1.D3_PWM
  N2: Q1.C, LED2.red_anode
  N3: Q2.B, Componente1.D5_PWM
  N4: Q2.C, LED2.blue_anode
  N5: Q3.B, Componente1.D7
  N6: Q3.C, LED2.green_anode
  N7: LED2.common_cathode, Componente1.D1/TX
  N8: Componente1.D9_PWM, Componente2.RST
  N9: Componente1.D10_PWM/SS, Componente2.SDA
  N10: Componente1.D11/MOSI, Componente2.MOSI
  N11: Componente1.D12/MISO, Componente2.MISO
  N12: Componente1.D13/SCK, Componente2.SCK
  5V: Componente1.5V, Componente2.3.3V

custom parts:
  RFID-RC522-v2: A simple China made RFID-RC522 Reader; do check the pin labels, as this is a MFRC522 based clone.
